# Fritzing sketch 3botones 2leds dht11 (saved by Fritzing 0.9.3b)
breadboards: 1

parts:
  E1 = ESP32-Cam
  S1 = Pushbutton [package="[THT]"]
  S2 = Pushbutton [package="[THT]"]
  S3 = Pushbutton [package="[THT]"]
  LED1 = LED - 5mm [color="Red (633nm)" package="5 mm [THT]"]
  LED2 = LED - 5mm [color="Red (633nm)" package="5 mm [THT]"]
  Mod1 = KY-015 Temperature & Humidity Sensor Module [package="Breakout board"]

nets:
  5V: E1.5V, Mod1.Vin
  N1: E1.GND#1, S1.Pin_3, S1.Pin_4, S2.Pin_3, S2.Pin_4, S3.Pin_3, S3.Pin_4, LED1.cathode, LED2.cathode, Mod1.-
  N2: E1.GPIO_12, Mod1.S
  N3: E1.GPIO_13, S3.Pin_1, S3.Pin_2
  N4: E1.GPIO_15, S1.Pin_1, S1.Pin_2
  N5: E1.GPIO_14, S2.Pin_1, S2.Pin_2
  N6: E1.GPIO_2, LED1.anode
  N7: E1.GPIO_16, LED2.anode

custom parts:
  KY-015 Temperature & Humidity Sensor Module: KY-015 temperature and humidity sensor module, provides a low-latency serial interface to measure humidity and temperature.
